# Fritzing sketch Untitled Sketch bd (saved by Fritzing 0.9.3b)
circuit board: 8.46667cm x 5.64444cm
breadboards: 1

parts:
  IC1 = L293D [package=THT]
  S1 = Pushbutton [package=THT]
  S2 = Pushbutton [package=THT]
  R1 = Resistor [tolerance=±5% resistance=220 package="2512 [SMD]"]
  R2 = Resistor [tolerance=±5% resistance=220 package="2512 [SMD]"]
  M1 = DC Motor

nets (from the schematic view):
  5V: IC1.Enable_1, IC1.+Vmotor, IC1.+V, S1.leg1, S2.leg1
  N1: IC1.In_1, S1.leg0, R1.Pin_0
  N2: IC1.Out_1_(_Controlled_by_Enable_1_), M1.pin_1
  GND: IC1.0V, R1.Pin_1, R2.Pin_1
  N3: IC1.Out_2_(_Controlled_by_Enable_1_), M1.pin_2
  N4: IC1.In_2, S2.leg0, R2.Pin_0
